# Fritzing sketch diy-midi-controller (saved by Fritzing 1.0.2b)
breadboards: 7

parts:
  Arduino_Pro_Micro = Arduino Micro (Rev3)
  Part2 = Analog Digital MUX Breakout
  R1 = Rotary Potentiometer (Small) [maximum_resistance=10kΩ knob_status=50% power=0.5W package=THT]
  R2 = Rotary Potentiometer (Small) [maximum_resistance=10kΩ knob_status=50% power=0.5W package=THT]
  R3 = Rotary Potentiometer (Small) [maximum_resistance=10kΩ knob_status=50% power=0.5W package=THT]
  R4 = Rotary Potentiometer (Small) [maximum_resistance=10kΩ knob_status=50% power=0.5W package=THT]
  R5 = Rotary Potentiometer (Small) [maximum_resistance=10kΩ knob_status=50% power=0.5W package=THT]
  R6 = Rotary Potentiometer (Small) [maximum_resistance=10kΩ knob_status=50% power=0.5W package=THT]
  R7 = Rotary Potentiometer (Small) [maximum_resistance=10kΩ knob_status=50% power=0.5W package=THT]
  R8 = Rotary Potentiometer (Small) [maximum_resistance=10kΩ knob_status=50% power=0.5W package=THT]
  R9 = Rotary Potentiometer (Small) [maximum_resistance=10kΩ knob_status=50% power=0.5W package=THT]
  R10 = Rotary Potentiometer (Small) [maximum_resistance=10kΩ knob_status=50% power=0.5W package=THT]
  R11 = Rotary Potentiometer (Small) [maximum_resistance=10kΩ knob_status=50% power=0.5W package=THT]
  R12 = Rotary Potentiometer (Small) [maximum_resistance=10kΩ knob_status=50% power=0.5W package=THT]
  R13 = Rotary Potentiometer (Small) [maximum_resistance=10kΩ knob_status=50% power=0.5W package=THT]
  R14 = Rotary Potentiometer (Small) [maximum_resistance=10kΩ knob_status=50% power=0.5W package=THT]
  R15 = Rotary Potentiometer (Small) [maximum_resistance=10kΩ knob_status=50% power=0.5W package=THT]
  R16 = Rotary Potentiometer (Small) [maximum_resistance=10kΩ knob_status=50% power=0.5W package=THT]
  Part3 = Analog Digital MUX Breakout
  R17 = Rotary Potentiometer (Small) [maximum_resistance=10kΩ knob_status=50% power=0.5W package=THT]
  R18 = Rotary Potentiometer (Small) [maximum_resistance=10kΩ knob_status=50% power=0.5W package=THT]
  R19 = Rotary Potentiometer (Small) [maximum_resistance=10kΩ knob_status=50% power=0.5W package=THT]
  R20 = Rotary Potentiometer (Small) [maximum_resistance=10kΩ knob_status=50% power=0.5W package=THT]
  R21 = Rotary Potentiometer (Small) [maximum_resistance=10kΩ knob_status=50% power=0.5W package=THT]
  R22 = Rotary Potentiometer (Small) [maximum_resistance=10kΩ knob_status=50% power=0.5W package=THT]
  R23 = Rotary Potentiometer (Small) [maximum_resistance=10kΩ knob_status=50% power=0.5W package=THT]
  R24 = Rotary Potentiometer (Small) [maximum_resistance=10kΩ knob_status=50% power=0.5W package=THT]
  S1 = Pushbutton [package="[THT]"]
  S2 = Pushbutton [package="[THT]"]
  S3 = Pushbutton [package="[THT]"]
  S4 = Pushbutton [package="[THT]"]
  S5 = Pushbutton [package="[THT]"]
  S6 = Pushbutton [package="[THT]"]
  S7 = Pushbutton [package="[THT]"]
  S8 = Pushbutton [package="[THT]"]
  Part4 = Analog Digital MUX Breakout
  S9 = Pushbutton [package="[THT]"]
  S10 = Pushbutton [package="[THT]"]
  S11 = Pushbutton [package="[THT]"]
  S12 = Pushbutton [package="[THT]"]
  S13 = Pushbutton [package="[THT]"]
  S14 = Pushbutton [package="[THT]"]
  S15 = Pushbutton [package="[THT]"]
  S16 = Pushbutton [package="[THT]"]
  S17 = Pushbutton [package="[THT]"]
  S18 = Pushbutton [package="[THT]"]
  S19 = Pushbutton [package="[THT]"]
  S20 = Pushbutton [package="[THT]"]
  S21 = Pushbutton [package="[THT]"]
  S22 = Pushbutton [package="[THT]"]
  S23 = Pushbutton [package="[THT]"]
  S24 = Pushbutton [package="[THT]"]

nets:
  N1: Arduino_Pro_Micro.GND, R1.leg1, R2.leg1, R3.leg1, R4.leg1, R5.leg1, R6.leg1, R7.leg1, R8.leg1, R9.leg1, R10.leg1, R11.leg1, R12.leg1, R13.leg1, R14.leg1, R15.leg1, R16.leg1, R17.leg1, R18.leg1, R19.leg1, R20.leg1, R21.leg1, R22.leg1, R23.leg1, S1.Pin_3, S1.Pin_4, S2.Pin_3, S2.Pin_4, S3.Pin_3, S3.Pin_4, S4.Pin_3, S4.Pin_4, S5.Pin_3, S5.Pin_4, S6.Pin_3, S6.Pin_4, S7.Pin_3, S7.Pin_4, S8.Pin_3, S8.Pin_4, S9.Pin_3, S9.Pin_4, S10.Pin_3, S10.Pin_4, S11.Pin_3, S11.Pin_4, S12.Pin_3, S12.Pin_4, S13.Pin_3, S13.Pin_4, S14.Pin_3, S14.Pin_4, S15.Pin_3, S15.Pin_4, S16.Pin_3, S16.Pin_4, S17.Pin_3, S17.Pin_4, S18.Pin_3, S18.Pin_4, S19.Pin_3, S19.Pin_4, S20.Pin_3, S20.Pin_4, S21.Pin_3, S21.Pin_4, S22.Pin_3, S22.Pin_4, S23.Pin_3, S23.Pin_4, S24.Pin_3, S24.Pin_4
  N2: Arduino_Pro_Micro.5V, R1.leg2, R2.leg2, R3.leg2, R4.leg2, R5.leg2, R6.leg2, R7.leg2, R8.leg2, R9.leg2, R10.leg2, R11.leg2, R12.leg2, R13.leg2, R14.leg2, R15.leg2, R16.leg2, R17.leg2, R18.leg2, R19.leg2, R20.leg2, R21.leg2, R22.leg2, R23.leg2, R24.leg1, R24.leg2
  N3: Part2.C0, R1.wiper
  N4: Part2.C1, R2.wiper
  N5: Part2.C2, R3.wiper
  N6: Part2.C3, R4.wiper
  N7: Part2.C4, R5.wiper
  N8: Part2.C5, R6.wiper
  N9: Part2.C6, R7.wiper
  N10: Part2.C7, R8.wiper
  N11: Part2.C8, R9.wiper
  N12: Part2.C9, R10.wiper
  N13: Part2.C10, R11.wiper
  N14: Part2.C11, R12.wiper
  N15: Part2.C12, R13.wiper
  N16: Part2.C13, R14.wiper
  N17: Part2.C14, R15.wiper
  N18: Part2.C15, R16.wiper
  N19: Part2.S0, Part3.S0, Part4.S0
  N20: Part2.S1, Part3.S1, Part4.S1
  N21: Part2.S2, Part3.S2, Part4.S2
  N22: Part2.S3, Part3.S3, Part4.S3
  N23: Part3.C0, R20.wiper
  N24: Part3.C1, R18.wiper
  N25: Part3.C2, R24.wiper
  N26: Part3.C3, R23.wiper
  N27: Part3.C4, R19.wiper
  N28: Part3.C5, R21.wiper
  N29: Part3.C6, R17.wiper
  N30: Part3.C7, R22.wiper
  N31: Part3.C8, S1.Pin_1, S1.Pin_2
  N32: Part3.C9, S2.Pin_1, S2.Pin_2
  N33: Part3.C10, S3.Pin_1, S3.Pin_2
  N34: Part3.C11, S4.Pin_1, S4.Pin_2
  N35: Part3.C12, S5.Pin_1, S5.Pin_2
  N36: Part3.C13, S6.Pin_1, S6.Pin_2
  N37: Part3.C14, S7.Pin_1, S7.Pin_2
  N38: Part3.C15, S8.Pin_1, S8.Pin_2
  N39: Part4.C0, S9.Pin_1, S9.Pin_2
  N40: Part4.C1, S10.Pin_1, S10.Pin_2
  N41: Part4.C2, S11.Pin_1, S11.Pin_2
  N42: Part4.C3, S12.Pin_1, S12.Pin_2
  N43: Part4.C4, S13.Pin_1, S13.Pin_2
  N44: Part4.C5, S14.Pin_1, S14.Pin_2
  N45: Part4.C6, S15.Pin_1, S15.Pin_2
  N46: Part4.C7, S16.Pin_1, S16.Pin_2
  N47: Part4.C8, S17.Pin_1, S17.Pin_2
  N48: Part4.C9, S18.Pin_1, S18.Pin_2
  N49: Part4.C10, S19.Pin_1, S19.Pin_2
  N50: Part4.C11, S20.Pin_1, S20.Pin_2
  N51: Part4.C12, S21.Pin_1, S21.Pin_2
  N52: Part4.C13, S22.Pin_1, S22.Pin_2
  N53: Part4.C14, S23.Pin_1, S23.Pin_2
  N54: Part4.C15, S24.Pin_1, S24.Pin_2

// code stored in the sketch: midi-controller.ino

